// Logisim project LC-3-v0.circ as structural Verilog: 18 circuits, main circuit DecodeIR
// RES
module main (
  input  Reset,
  output out_2,
  output out_3,
  output out_4,
  output out_5,
  output out_6,
  output out_7,
  output out_8,
  output [15:0] out_9,
  output [15:0] out_10,
  output [15:0] out_11,
  output [15:0] out_12,
  output [15:0] out_13,
  output [15:0] out_14,
  output [15:0] out_15,
  output [15:0] out_16,
  output [15:0] out_17,
  output halt,
  output [15:0] out_19,
  output [15:0] out_20,
  output [15:0] out_21,
  output [15:0] out_22
);

  wire decodeir_1_writereg, getcst_1_usecst, or16_1_out_2, or16_2_out_2, ramctrl_1_memload,
       ramctrl_1_memstore;
  wire [2:0] nzp_1_nzp;
  wire [15:0] alu_1_output, getcst_1_cst, RegIN, registres_1_out_sr1, registres_1_out_sr2;

  BiClock biclock_1 (.reset(Reset), .signal0(out_2), .signal1(out_3));
  RegPC regpc_1 (
    .H(out_3), .PC(out_9), .Reset(Reset), .IR(out_10), .R(registres_1_out_sr1), .TestNZP(out_5), .Jump(out_4));
  // Probe on out_9
  // Probe on out_11
  GetAddr getaddr_1 (.PC(out_9), .BaseR(registres_1_out_sr1), .IR(out_10), .Addr(out_11), .Fetch(out_2));
  // Probe on out_12
  LED led_1 (.in(out_6));
  RamCtrl ramctrl_1 (
    .Store(out_7), .Fetch(out_2), .Exec(out_3), .Load(out_6), .MemStore(ramctrl_1_memstore),
    .MemLoad(ramctrl_1_memload));
  LED led_2 (.in(out_7));
  // Probe on out_13
  RAM #(.addrWidth(16), .dataWidth(16), .bus("separate")) ram_1 (
    .addr(out_11), .din(out_12), .data(out_13), .str(ramctrl_1_memstore), .clk(ramctrl_1_memstore),
    .ld(ramctrl_1_memload));  // open: sel, clr
  Register #(.width(16), .trigger("falling")) RegIR (.D(out_13), .Q(out_10), .clk(out_2));  // open: en, clr
  DecodeIR decodeir_1 (.IR(out_10), .Jump(out_4), .WriteReg(decodeir_1_writereg), .Load(out_6), .Store(out_7));
  // Probe on out_10[11:9]
  // Probe on out_10[8:6]
  // Probe on out_10[2:0]
  // Probe on getcst_1_cst
  GetCst getcst_1 (.IR(out_10), .Cst(getcst_1_cst), .UseCst(getcst_1_usecst));
  // Probe on out_10[15:14]
  and and_1 (out_8, decodeir_1_writereg, out_3);
  Registres registres_1 (
    .SR1(out_10[8:6]), .IN(RegIN), .SR2(out_10[2:0]), .WriteReg(out_8), .DR_SR(out_10[11:9]),
    .OUT_SR1(registres_1_out_sr1), .OUT_SR2(registres_1_out_sr2), .OUT_SR(out_12), .R0(out_14), .R1(out_15),
    .R2(out_16), .R3(out_17), .R4(out_19), .R5(out_20), .R6(out_21), .R7(out_22));
  // Probe on registres_1_out_sr1
  ALU alu_1 (
    .UseCst(getcst_1_usecst), .e2(out_10[15:14]), .Input1(registres_1_out_sr1), .Input2(registres_1_out_sr2),
    .Cst(getcst_1_cst), .Output(alu_1_output));
  // Probe on registres_1_out_sr2
  // Probe on alu_1_output
  NZP nzp_1 (.RES(RegIN), .NZP(nzp_1_nzp), .IR(out_10), .TestNZP(out_5), .WriteReg(out_8));
  // Probe on nzp_1_nzp
  Or16 or16_1 (.in_1(out_10), .out_2(or16_1_out_2));
  Or16 or16_2 (.in_1(out_9), .out_2(or16_2_out_2));
  // Probe on out_14
  // Probe on out_15
  // Probe on out_16
  // Probe on out_17
  // Probe on out_19
  // Probe on out_20
  // Probe on out_21
  // Probe on out_22
  and and_2 (halt, ~or16_1_out_2, or16_2_out_2);  // AND_Gate
  WriteVal writeval_1 (
    .Load(out_6), .ALURes(alu_1_output), .MemOUT(out_13), .IR(out_10), .PC(out_9), .RegIN(RegIN));  // open: out_7

  // Other names for the same wires on the sheet: Addr[15:0] = out_11; Condition = out_5; Exec = out_3; Fetch = out_2;
  //   IR[15:0] = out_10; JumpInstr = out_4; Load = out_6; MemIN[15:0] = out_12; MemOUT[15:0] = out_13;
  //   PC[15:0] = out_9; R0[15:0] = out_14; R1[15:0] = out_15; R2[15:0] = out_16; R3[15:0] = out_17; R4[15:0] = out_19;
  //   R5[15:0] = out_20; R6[15:0] = out_21; R7[15:0] = out_22; Store = out_7; WriteReg = out_8

  // Notes on the sheet:
  //   R
  //   IR
  //   R
  //   IR
  //   RAM
  //   Traces (NE PAS MODIFIER)______________________________________________________________________________________________________
  //   GetOp
  //   Arret des traces au 1er NOP
endmodule

module ALU (
  input  [15:0] Input1,
  input  [15:0] Input2,
  input  [15:0] Cst,
  input  UseCst,
  input  [1:0] e2,
  output [15:0] Output
);

  wire [15:0] adder_1_out, and_1_out, multiplexer_1_out, popcnt_1_out_2, xor_1_out;

  Multiplexer #(.width(16), .enable("false")) multiplexer_1 (
    .in0(Input2), .in1(Cst), .out(multiplexer_1_out), .sel(UseCst));
  Adder #(.width(16)) adder_1 (.a(multiplexer_1_out), .b(Input1), .out(adder_1_out));  // open: cin, cout
  assign and_1_out = Input1 & multiplexer_1_out;  // AND_Gate and_1, 16 bits wide
  Multiplexer #(.select(2), .width(16), .enable("false")) multiplexer_2 (
    .in0(adder_1_out), .in1(and_1_out), .in2(xor_1_out), .in3(popcnt_1_out_2), .out(Output), .sel(e2));
  assign xor_1_out = Input1 ^ multiplexer_1_out;  // XOR_Gate xor_1, 16 bits wide
  popcnt popcnt_1 (.in_1(Input1), .out_2(popcnt_1_out_2));

  // Notes on the sheet:
  //   le not semble être un cas particulier du XOR car quand on fait le xor avec un immédiat de 5 bits tous à 1,
  //   ça revient à renvoyer 1 uniquement si tous les bits sont renversé donc le NOT
  //   A COMPLETER v1
endmodule

module DecodeIR (
  input  [15:0] IR,
  output Load,
  output WriteReg,
  output Jump,
  output Store
);

  wire and_1_out, and_2_out, and_3_out, and_5_out, and_6_out, and_7_out, and_8_out, and_9_out;

  and and_1 (and_1_out, IR[12], ~IR[13]);  // AND_Gate
  and and_2 (and_2_out, ~IR[12], ~IR[13], IR[14], IR[15]);  // AND_Gate
  and and_3 (and_3_out, ~IR[12], ~IR[13], IR[14], ~IR[15]);  // AND_Gate
  and and_4 (Load, ~IR[12], IR[13]);  // AND_Gate
  and and_5 (and_5_out, ~IR[12], ~IR[13], ~IR[14], ~IR[15]);  // AND_Gate
  and and_6 (and_6_out, IR[12], IR[13], IR[14], IR[15]);
  or or_1 (Jump, and_5_out, and_2_out, and_3_out, and_6_out);
  or or_2 (WriteReg, Load, and_1_out, Jump);
  and and_7 (and_7_out, IR[12], IR[13], ~IR[14], ~IR[15]);  // AND_Gate
  and and_8 (and_8_out, IR[12], IR[13], IR[14], ~IR[15]);  // AND_Gate
  and and_9 (and_9_out, IR[12], IR[13], ~IR[14], IR[15]);  // AND_Gate
  // Probe on and_1_out
  or or_3 (Store, and_7_out, and_8_out, and_9_out);

  // Other names for the same wires on the sheet: _12 = IR[12]; _13 = IR[13]; _14 = IR[14]; _15 = IR[15]

  // Notes on the sheet:
  //   pour diff avec le nop faire un un xor sur 11,10,9 ?
  //   nop identique au xor c un cas particulier du BR
  //   Types d'instructions
  //   A COMPLETER v1 : toujours Arith pour l'instant
  //   Instruction modifiant les registres ?
  //   A COMPLETER v1 : toujours oui pour l'instant
endmodule

module BiClock (
  input  reset,
  output signal0,
  output signal1
);

  wire and_1_out, horloge_out, not_1_out, register_1_q;

  Clock horloge (.out(horloge_out));
  not not_1 (not_1_out, register_1_q);
  Register #(.width(1), .trigger("falling")) register_1 (
    .D(not_1_out), .Q(register_1_q), .clk(horloge_out), .clr(reset));  // open: en
  and and_1 (and_1_out, horloge_out, ~reset);  // AND_Gate
  and and_2 (signal0, ~register_1_q, and_1_out);  // AND_Gate
  and and_3 (signal1, register_1_q, and_1_out);

  // Notes on the sheet:
  //   Ce module divise une horloge en deux sous-horloges alternées
  //   Chronogrammes :
  //   horloge: 0101010101 signal0: 0100010001 signal1: 000100010
  //   registre 1-bit
  //   Enable
  //   select : 0 / 1
endmodule

module GetAddr (
  input  [15:0] IR,
  input  Fetch,
  input  [15:0] PC,
  input  [15:0] BaseR,
  output [15:0] Addr
);

  wire or_1_out;
  wire [15:0] adder_1_out, adder_2_out, multiplexer_1_out, offset6_1_off6, offset9_1_off9;

  Offset9 offset9_1 (.IR(IR), .Off9(offset9_1_off9));
  Offset6 offset6_1 (.IR(IR), .Off6(offset6_1_off6));
  Adder #(.width(16)) adder_1 (.a(offset6_1_off6), .b(BaseR), .out(adder_1_out));  // open: cin, cout
  Adder #(.width(16)) adder_2 (.a(offset9_1_off9), .b(PC), .out(adder_2_out), .cin(1'b1));  // open: cout
  Multiplexer #(.width(16), .disabled(0), .enable("false")) multiplexer_1 (
    .in0(adder_2_out), .in1(adder_1_out), .out(multiplexer_1_out), .sel(IR[14]));
  or or_1 (or_1_out, ~IR[13], Fetch);  // OR_Gate
  Multiplexer #(.width(16), .disabled(0), .enable("false")) multiplexer_2 (
    .in0(multiplexer_1_out), .in1(PC), .out(Addr), .sel(or_1_out));

  // Notes on the sheet:
  //   ici pour les load nous voyons bien l'addition qui permet
  //   de charger la bonne adresse (calcul de l'offset + pc + 1 afin
  //   d'obtenir la bonne adresse et pouvoir charger la valeur à cette
  //   adresse mémoire. C'est grace à cela que nous n'avons pas besoin
  //   de faire les additions nous mêmes
  //   PC+SEXT(Offset6)
  //   b14: label or BaseR?
  //   PC+SEXT(Offset9)
  //   b13: Load ou Store?
  //   Pourquoi ?
endmodule

module GetCst (
  input  [15:0] IR,
  output [15:0] Cst,
  output UseCst
);

  assign Cst = {{11{IR[4]}}, IR[4:0]};  // Bit_Extender bit_extender_1

  assign UseCst = IR[5];
endmodule

module NZP (
  input  [15:0] RES,
  input  [15:0] IR,
  input  WriteReg,
  output [2:0] NZP,
  output TestNZP
);

  wire and_1_out, and_2_out, and_3_out;
  wire [14:0] register_1_q;

  Register #(.width(16)) register_1 (.D(RES), .Q({NZP[2], register_1_q}), .clk(WriteReg));  // open: en, clr
  nor nor_1 (NZP[1], register_1_q[0], register_1_q[1], register_1_q[2], register_1_q[3], register_1_q[4], register_1_q[5], register_1_q[6], register_1_q[7], register_1_q[8], register_1_q[9], register_1_q[10], register_1_q[11], register_1_q[12], register_1_q[13], register_1_q[14], NZP[2]);
  nor nor_2 (NZP[0], NZP[1], NZP[2]);
  and and_1 (and_1_out, NZP[0], IR[9]);
  and and_2 (and_2_out, NZP[1], IR[10]);
  and and_3 (and_3_out, NZP[2], IR[11]);
  or or_1 (TestNZP, and_1_out, and_2_out, and_3_out);

  // Notes on the sheet:
  //   Entrées non utilisées pour l'instant
  //   (Resultat du calcul courant)
  //   (Instruction courante)
  //   si 1, instruction doit actualiser NZP
  //   Valeur actuelle du registre d'état NZP
  //   A COMPLETER v1 : pour l'instant toujours 000
  //   Test de saut : vrai si au moins un flag est vrai
  //   A COMPLETER v1 : pour l'instant toujours 0
endmodule

// Off6
module Offset6 (
  input  [15:0] IR,
  output [15:0] Off6
);

  assign Off6 = {{10{IR[5]}}, IR[5:0]};  // Bit_Extender bit_extender_1
endmodule

// Off9
module Offset9 (
  input  [15:0] IR,
  output [15:0] Off9
);

  assign Off9 = {{7{IR[8]}}, IR[8:0]};  // Bit_Extender bit_extender_1
endmodule

module Or16 (
  input  [15:0] in_1,
  output out_2
);

  wire [1:0] or_2_out;
  wire [7:0] or_1_out;

  assign or_1_out = in_1[7:0] | in_1[15:8];  // OR_Gate or_1, 8 bits wide
  assign or_2_out = or_1_out[1:0] | or_1_out[3:2] | or_1_out[5:4] | or_1_out[7:6];  // OR_Gate or_2, 2 bits wide
  or or_3 (out_2, or_2_out[0], or_2_out[1]);
endmodule

module RamCtrl (
  input  Exec,
  input  Fetch,
  input  Load,
  input  Store,
  output MemLoad,
  output MemStore
);

  wire and_1_out;

  and and_1 (and_1_out, Exec, Load);
  and and_2 (MemStore, Exec, Store);
  or or_1 (MemLoad, Fetch, and_1_out);
endmodule

module Registres (
  input  [2:0] SR1,
  input  [15:0] IN,
  input  [2:0] SR2,
  input  WriteReg,
  input  [2:0] DR_SR,
  output [15:0] R0,
  output [15:0] OUT_SR1,
  output [15:0] R1,
  output [15:0] R2,
  output [15:0] R3,
  output [15:0] OUT_SR2,
  output [15:0] R4,
  output [15:0] R5,
  output [15:0] OUT_SR,
  output [15:0] R6,
  output [15:0] R7
);

  wire decoder_1_out0, decoder_1_out1, decoder_1_out2, decoder_1_out3, decoder_1_out4, decoder_1_out5,
       decoder_1_out6, decoder_1_out7;

  Decoder #(.select(3), .disabled(0)) decoder_1 (
    .out0(decoder_1_out0), .out1(decoder_1_out1), .out2(decoder_1_out2), .out3(decoder_1_out3),
    .out4(decoder_1_out4), .out5(decoder_1_out5), .out6(decoder_1_out6), .out7(decoder_1_out7), .sel(DR_SR),
    .en(WriteReg));
  Register #(.width(16), .trigger("falling")) u_R0 (.D(IN), .Q(R0), .clk(decoder_1_out0));  // open: en, clr
  Register #(.width(16), .trigger("falling")) u_R1 (.D(IN), .Q(R1), .clk(decoder_1_out1));  // open: en, clr
  Register #(.width(16), .trigger("falling")) u_R2 (.D(IN), .Q(R2), .clk(decoder_1_out2));  // open: en, clr
  Register #(.width(16), .trigger("falling")) u_R3 (.D(IN), .Q(R3), .clk(decoder_1_out3));  // open: en, clr
  Register #(.width(16), .trigger("falling")) u_R4 (.D(IN), .Q(R4), .clk(decoder_1_out4));  // open: en, clr
  Register #(.width(16), .trigger("falling")) u_R5 (.D(IN), .Q(R5), .clk(decoder_1_out5));  // open: en, clr
  Register #(.width(16), .trigger("falling")) u_R6 (.D(IN), .Q(R6), .clk(decoder_1_out6));  // open: en, clr
  Register #(.width(16), .trigger("falling")) u_R7 (.D(IN), .Q(R7), .clk(decoder_1_out7));  // open: en, clr
  Multiplexer #(.select(3), .width(16), .enable("false")) multiplexer_1 (
    .in0(R0), .in1(R1), .in2(R2), .in3(R3), .in4(R4), .in5(R5), .in6(R6), .in7(R7), .out(OUT_SR1), .sel(SR1));
  Multiplexer #(.select(3), .width(16), .enable("false")) multiplexer_2 (
    .in0(R0), .in1(R1), .in2(R2), .in3(R3), .in4(R4), .in5(R5), .in6(R6), .in7(R7), .out(OUT_SR2), .sel(SR2));
  Multiplexer #(.select(3), .width(16), .enable("false")) multiplexer_3 (
    .in0(R0), .in1(R1), .in2(R2), .in3(R3), .in4(R4), .in5(R5), .in6(R6), .in7(R7), .out(OUT_SR), .sel(DR_SR));
endmodule

module RegPC (
  input  [15:0] IR,
  input  H,
  input  [15:0] R,
  input  Reset,
  input  Jump,
  input  TestNZP,
  output [15:0] PC
);

  wire and_1_out, and_2_out, or_1_out;
  wire [15:0] adder_1_out, adder_2_out, multiplexer_1_out, multiplexer_2_out, multiplexer_3_out,
       offset9_1_off9;

  Offset9 offset9_1 (.IR(IR), .Off9(offset9_1_off9));
  and and_1 (and_1_out, IR[14], Jump);
  and and_2 (and_2_out, Jump, TestNZP);
  Adder #(.width(16)) adder_1 (.a(PC), .b(16'h1), .out(adder_1_out));  // open: cin, cout
  Multiplexer #(.width(16), .disabled(0), .enable("false")) multiplexer_1 (
    .in0(offset9_1_off9), .in1({16{1'b0}}), .out(multiplexer_1_out), .sel(and_1_out));
  or or_1 (or_1_out, and_1_out, and_2_out);
  Adder #(.width(16)) adder_2 (.a(adder_1_out), .b(multiplexer_1_out), .out(adder_2_out));  // open: cin, cout
  Multiplexer #(.width(16), .disabled(0), .enable("false")) multiplexer_2 (
    .in0(adder_2_out), .in1(R), .out(multiplexer_2_out), .sel(and_1_out));
  Multiplexer #(.width(16), .enable("false")) multiplexer_3 (
    .in0(adder_1_out), .in1(multiplexer_2_out), .out(multiplexer_3_out), .sel(or_1_out));
  Register #(.width(16), .trigger("falling")) u_PC (.D(multiplexer_3_out), .Q(PC), .clk(H), .clr(Reset));  // open: en

  // Notes on the sheet:
  //   A COMPLETER v2
  //   JSR ssi JMP et 14
  //   pour BR
  //   pour JSR
  //   PC <- PC + 1
  //   BaseR
  //   BaseR ssi JMP ou JSRR
  //   A COMPLETER v2
  //   saut ssi JMP et (BR =>TestNZP)
  //   PC+Off
  //   pas saut
  //   saut
endmodule

module Offset11 (
  input  [15:0] IR,
  output [15:0] SEXTOff11
);

  assign SEXTOff11 = {{5{1'b0}}, IR[10:0]};  // Bit_Extender bit_extender_1
endmodule

module WriteVal (
  input  Load,
  input  [15:0] ALURes,
  input  [15:0] MemOUT,
  input  [15:0] IR,
  input  [15:0] PC,
  output [15:0] RegIN,
  output [1:0] out_7
);

  wire JSR, LEA;
  wire [15:0] adder_1_out, adder_2_out, offset9_1_off9;

  Offset9 offset9_1 (.IR(IR), .Off9(offset9_1_off9));
  Adder #(.width(16)) adder_1 (.a(PC), .b(16'h1), .out(adder_1_out));  // open: cin, cout
  and and_1 (LEA, ~IR[12], IR[13], IR[14], IR[15]);  // AND_Gate
  and and_2 (JSR, ~IR[12], ~IR[13], IR[14], ~IR[15]);  // AND_Gate
  Adder #(.width(16)) adder_2 (.a(adder_1_out), .b(offset9_1_off9), .out(adder_2_out));  // open: cin, cout
  Multiplexer #(.select(2), .width(16)) multiplexer_1 (
    .in0(ALURes), .in1(MemOUT), .in2(adder_2_out), .in3(adder_1_out), .out(RegIN), .sel(out_7), .en(1'b1));
  Adder #(.width(2)) adder_3 (.a({1'b0, LEA}), .b({2{JSR}}), .out(out_7), .cin(Load));  // open: cout

  // Notes on the sheet:
  //   ici je veux récuperer les 9 premiers bits pour calculer l'offset pour pc+offset 
  //   solution pour pouvoir séléctionner la bonne sortie 
  //   en fonction du résultat de JSR, LEA, LOAD et le cas par défaut pour ALUres
  //   comme LEA est un load on fait l'addition de 1+1 qui vaut 2 et on à donc la seconde sortie du MUX
  //   Ici, il faut incrémenter PC de 1 car au moment d'arriver sur l'instruction, on à pas encore
  //   pu incrémenter PC de 1 car nous sommes au début du cycle donc le circuit n'a pas
  //   pu incrémenter PC, c'est après le fetch dans RamCtrl que ça change
  //   contrairement aux autres load, lea est un cas spécial car il ne va pas lire de la mémoire
  //   il va plutôt stocker la mémoire dans un registre donc on le différencie en terme de sortie
  //   addition meme pour pc simple ?
  //   A COMPLETER v1 et v2 :
  //   RegIN = si JSR alors PC sinon si LEA alors PC+SEXT(Offset9) sinon si Load alors MemOUT sinon ALURes  
endmodule

module popcnt4 (
  input  [3:0] a,
  output [3:0] out_2
);

  wire adder_1_out, adder_2_out;
  wire [0:0] adder_4_out;
  wire [3:0] adder_3_out, adder_5_out, adder_6_out;

  Adder #(.width(1)) adder_1 (.a(a[0]), .b(1'b0), .out(adder_1_out));  // open: cin, cout
  Adder #(.width(1)) adder_2 (.a(a[3]), .b(1'b0), .out(adder_2_out));  // open: cin, cout
  Adder #(.width(1)) adder_3 (.a(1'b0), .b(a[1]), .out(adder_3_out[0]));  // open: cin, cout
  Adder #(.width(1)) adder_4 (.a(a[2]), .b(1'b0), .out(adder_4_out[0]));  // open: cin, cout
  not not_1 (adder_3_out[3], 1'b1);
  Adder #(.width(4)) adder_5 (
    .a(4'b0000), .b({{3{adder_3_out[3]}}, adder_3_out[0]}), .out(adder_5_out), .cin(adder_1_out));  // open: cout
  Adder #(.width(4)) adder_6 (
    .a({{3{adder_3_out[3]}}, adder_4_out[0]}), .b(4'b0000), .out(adder_6_out), .cin(adder_2_out));  // open: cout
  Adder #(.width(4)) adder_7 (.a(adder_5_out), .b(adder_6_out), .out(out_2));  // open: cin, cout
endmodule

module popcnt8 (
  input  [7:0] a,
  output [3:0] out_2
);

  wire [3:0] popcnt4_1_out_2, popcnt4_2_out_2;

  popcnt4 popcnt4_1 (.a(a[3:0]), .out_2(popcnt4_1_out_2));
  popcnt4 popcnt4_2 (.a(a[7:4]), .out_2(popcnt4_2_out_2));
  Adder #(.width(4)) adder_1 (.a(popcnt4_1_out_2), .b(popcnt4_2_out_2), .out(out_2));  // open: cin, cout
endmodule

module popcnt (
  input  [15:0] in_1,
  output [15:0] out_2
);

  wire [3:0] popcnt8_1_out_2, popcnt8_2_out_2;

  popcnt8 popcnt8_1 (.a(in_1[7:0]), .out_2(popcnt8_1_out_2));
  popcnt8 popcnt8_2 (.a(in_1[15:8]), .out_2(popcnt8_2_out_2));
  Adder #(.width(16)) adder_1 (
    .a({{12{1'b0}}, popcnt8_1_out_2}), .b({{12{1'b0}}, popcnt8_2_out_2}), .out(out_2));  // open: cin, cout
endmodule
